// Logisim project Datapath.circ as structural Verilog: 2 circuits, main circuit main
module main (
  input  in_1,
  input  in_2
);

  wire AluSrc, and_1_out, and_2_out, Bne, Branch, clock_1_out, Jump, JumpRegister, Link, MemRead, MemToReg,
       MemWrite, multiplexer_4_out, not_1_out, not_2_out, RegDst, WriteReg, zero;
  wire [1:0] main_1_aluop;
  wire [4:0] decodificador_1_rd, decodificador_1_rs, decodificador_1_rt, multiplexer_5_out,
       multiplexer_6_out, Op, shamt;
  wire [5:0] decodificador_1_func, OpCode;
  wire [15:0] decodificador_1_imm;
  wire [25:0] decodificador_1_addr;
  wire [31:0] adder_1_out, datamem_1_dados_lidos, extensor_sinal_1_saida, LD1, main_3_ld2, main_4_result,
       meminstr_1_instruction, multiplexer_1_out, multiplexer_2_out, multiplexer_3_out, multiplexer_7_out,
       multiplexer_8_out, multiplexer_9_out, PC, pc___4, pseudodireto_1_saida, shifter_1_out;

  // Probe on multiplexer_3_out
  Multiplexer #(.width(32), .enable("false")) multiplexer_1 (
    .in0(multiplexer_3_out), .in1(LD1), .out(multiplexer_1_out), .sel(JumpRegister));
  // Probe on pseudodireto_1_saida
  Multiplexer #(.width(32), .enable("false")) multiplexer_2 (
    .in0(multiplexer_1_out), .in1(pseudodireto_1_saida), .out(multiplexer_2_out), .sel(Jump));
  pseudodireto pseudodireto_1 (.PC(PC), .Saida(pseudodireto_1_saida), .addr(decodificador_1_addr));
  // Probe on multiplexer_2_out
  // Probe on extensor_sinal_1_saida
  Multiplexer #(.width(32), .enable("false")) multiplexer_3 (
    .in0(pc___4), .in1(adder_1_out), .out(multiplexer_3_out), .sel(and_1_out));
  Multiplexer #(.enable("false")) multiplexer_4 (.in0(zero), .in1(not_1_out), .out(multiplexer_4_out), .sel(Bne));
  not not_1 (not_1_out, zero);
  Register #(.width(32)) u_PC (.D(multiplexer_2_out), .en(1'b1), .Q(PC), .clk(clock_1_out), .clr(in_1));
  Clock clock_1 (.out(clock_1_out));
  Shifter #(.width(32)) shifter_1 (.in(extensor_sinal_1_saida), .\dist (5'b00010), .out(shifter_1_out));
  Adder #(.width(32)) adder_1 (.a(shifter_1_out), .b(pc___4), .out(adder_1_out));  // open: cin, cout
  and and_1 (and_1_out, multiplexer_4_out, Branch);
  Adder #(.width(32)) adder_2 (.a(32'h4), .b(PC), .out(pc___4));  // open: cin, cout
  MemInstr meminstr_1 (.PC_address(PC), .Instruction(meminstr_1_instruction));
  // Probe on meminstr_1_instruction
  // Probe on decodificador_1_func
  UC_main main_1 (
    .ALUOp(main_1_aluop), .RegDst(RegDst), .WriteReg(WriteReg), .ALUSrc(AluSrc), .MemToReg(MemToReg),
    .MemRead(MemRead), .MemWrite(MemWrite), .Branch(Branch), .Bne(Bne), .Jump(Jump), .Link(Link),
    .OpCode(OpCode));
  extensor_sinal extensor_sinal_1 (.entrada(decodificador_1_imm), .saida(extensor_sinal_1_saida));
  decodificador decodificador_1 (
    .\INSTRUÇÃO (meminstr_1_instruction), .FUNC(decodificador_1_func), .SHAMT(shamt),
    .RD(decodificador_1_rd), .RT(decodificador_1_rt), .RS(decodificador_1_rs), .OP_CODE(OpCode),
    .ADDR(decodificador_1_addr), .IMM(decodificador_1_imm));
  UCA_main main_2 (
    .funct(decodificador_1_func), .JumpRegister(JumpRegister), .Op(Op), .ALUOp(main_1_aluop), .OpCode(OpCode));
  Multiplexer #(.width(5), .enable("false")) multiplexer_5 (
    .in0(decodificador_1_rt), .in1(decodificador_1_rd), .out(multiplexer_5_out), .sel(RegDst));
  Registers_Bank_main main_3 (
    .LR1(decodificador_1_rs), .LR2(decodificador_1_rt), .WD(multiplexer_8_out), .RegWrite(and_2_out),
    .WR(multiplexer_6_out), .LD1(LD1), .LD2(main_3_ld2), .Clock(clock_1_out), .Clear(in_1));
  Multiplexer #(.width(5), .enable("false")) multiplexer_6 (
    .in0(multiplexer_5_out), .in1({5{1'b1}}), .out(multiplexer_6_out), .sel(Link));
  and and_2 (and_2_out, not_2_out, WriteReg);
  not not_2 (not_2_out, JumpRegister);
  Multiplexer #(.width(32), .enable("false")) multiplexer_7 (
    .in0(main_3_ld2), .in1(extensor_sinal_1_saida), .out(multiplexer_7_out), .sel(AluSrc));
  // Probe on LD1
  // Probe on multiplexer_7_out
  Multiplexer #(.width(32), .enable("false")) multiplexer_8 (
    .in0(multiplexer_9_out), .in1(pc___4), .out(multiplexer_8_out), .sel(Link));
  // Probe on main_3_ld2
  Multiplexer #(.width(32), .enable("false")) multiplexer_9 (
    .in0(main_4_result), .in1(datamem_1_dados_lidos), .out(multiplexer_9_out), .sel(MemToReg));
  // Probe on main_4_result
  ULA_main main_4 (
    .Result(main_4_result), .\Operação_ALU (Op), .SHAMT(shamt), .Zero(zero), .Entrada_A(LD1),
    .Entrada_B(multiplexer_7_out));  // open: Overflow
  datamem datamem_1 (
    .\Endereço (main_4_result), .Escreve_dado(main_3_ld2), .Dados_lidos(datamem_1_dados_lidos),
    .MemWrite(MemWrite), .MemRead(MemRead), .clk(clock_1_out), .clear(in_2));

  // Other names for the same wires on the sheet: Reset = in_1
endmodule

module pseudodireto (
  input  [25:0] addr,
  input  [31:0] PC,
  output [31:0] Saida
);

  // Probe on addr
  Shifter #(.width(26)) shifter_1 (.in(addr), .\dist (5'b00010), .out(Saida[25:0]));
  // Probe on Saida[25:0]

  assign Saida[31:26] = PC[31:26];
endmodule
