// Logisim project UC.circ as structural Verilog: 1 circuit, main circuit main
module main (
  input  [5:0] OpCode,
  output [1:0] ALUOp,
  output RegDst,
  output WriteReg,
  output ALUSrc,
  output MemToReg,
  output MemRead,
  output MemWrite,
  output Branch,
  output Bne,
  output Jump,
  output Link
);

  wire ADDI_out, BEQ_out, J_out, JR_out, R_out;

  and R (R_out, ~OpCode[5], ~OpCode[4], ~OpCode[3], ~OpCode[2], ~OpCode[1], ~OpCode[0]);  // AND_Gate
  and ADDI (ADDI_out, ~OpCode[5], ~OpCode[4], OpCode[3], ~OpCode[2], ~OpCode[1], ~OpCode[0]);  // AND_Gate
  and LW (MemRead, OpCode[5], ~OpCode[4], ~OpCode[3], ~OpCode[2], OpCode[1], OpCode[0]);  // AND_Gate
  and SW (MemWrite, OpCode[5], ~OpCode[4], OpCode[3], ~OpCode[2], OpCode[1], OpCode[0]);  // AND_Gate
  and BEQ (BEQ_out, ~OpCode[5], ~OpCode[4], ~OpCode[3], OpCode[2], ~OpCode[1], ~OpCode[0]);  // AND_Gate
  and u_BNE (Bne, ~OpCode[5], ~OpCode[4], ~OpCode[3], OpCode[2], ~OpCode[1], OpCode[0]);  // AND_Gate
  and J (J_out, ~OpCode[5], ~OpCode[4], ~OpCode[3], ~OpCode[2], OpCode[1], ~OpCode[0]);  // AND_Gate
  and JAL (Link, ~OpCode[5], ~OpCode[4], ~OpCode[3], ~OpCode[2], OpCode[1], OpCode[0]);  // AND_Gate
  and JR (JR_out, ~OpCode[5], ~OpCode[4], ~OpCode[3], ~OpCode[2], ~OpCode[1], ~OpCode[0]);  // AND_Gate
  or or_1 (ALUOp[1], BEQ_out, Bne);
  and and_1 (ALUOp[0], ~ALUOp[1], ~R_out);  // AND_Gate
  and and_2 (RegDst, ~MemRead, R_out);  // AND_Gate
  or or_2 (WriteReg, R_out, ADDI_out, MemRead, Link);
  or or_3 (ALUSrc, ADDI_out, MemRead, MemWrite);
  or or_4 (Branch, BEQ_out, Bne);
  or or_5 (Jump, J_out, Link);

  assign MemToReg = MemRead;

  // Notes on the sheet:
  //   R
  //   ADDI
  //   ORDEM DOS FIOS
  //   LW
  //   BEQ
  //   SW
  //   000000
  //   001000
  //   100011
  //   101011
  //   000100
  //   000101
  //   000010
  //   000011
  //   BNE
  //   J
  //   JAL
  //   ALUOp
  //   00 - FUNC
  //   01 - ADD
  //   10 - SUB
endmodule
