// Logisim project UCA.circ as structural Verilog: 1 circuit, main circuit main
module main (
  input  [5:0] funct,
  input  [5:0] OpCode,
  input  [1:0] ALUOp,
  output JumpRegister,
  output [4:0] Op
);

  wire and_1_out, R;

  and and_1 (and_1_out, ~funct[5], ~funct[4], funct[3], ~funct[2], ~funct[1], ~funct[0]);  // AND_Gate
  and and_2 (JumpRegister, and_1_out, R);
  Multiplexer #(.select(2), .width(5), .disabled(0), .enable("false")) multiplexer_1 (
    .in0({funct[5], funct[3:0]}), .in1(5'b10000), .in2(5'b10010), .out(Op), .sel(ALUOp));  // open: in3
  and and_3 (R, ~OpCode[0], ~OpCode[1], ~OpCode[2], ~OpCode[3], ~OpCode[4], ~OpCode[5]);  // AND_Gate

  // Notes on the sheet:
  //   ADD
  //   SUB
endmodule
