// Logisim project ULA.circ as structural Verilog: 1 circuit, main circuit main
module main (
  input  [4:0] \Operação_ALU ,
  input  [31:0] Entrada_A,
  input  [31:0] Entrada_B,
  input  [4:0] SHAMT,
  output [31:0] Result,
  output Zero,
  output Overflow
);

  wire adder_1_cout, and_4_out, and_5_out, isSub, isSum, or_2_out, or_3_out, subtractor_1_bout;
  wire [0:0] SLT;
  wire [31:0] AND, NOR, OR, SLL, SRL, subResult, sumResult, XOR;

  Comparator #(.width(32)) comparator_1 (.a(Entrada_A), .b(Entrada_B), .lt(SLT[0]));  // open: gt, eq
  assign AND = Entrada_A & Entrada_B;  // AND_Gate AND, 32 bits wide
  assign OR = Entrada_A | Entrada_B;  // OR_Gate OR, 32 bits wide
  assign NOR = ~(Entrada_A | Entrada_B);  // NOR_Gate NOR, 32 bits wide
  assign XOR = Entrada_A ^ Entrada_B;  // XOR_Gate XOR, 32 bits wide
  Adder #(.width(32)) adder_1 (.a(Entrada_A), .b(Entrada_B), .out(sumResult), .cout(adder_1_cout));  // open: cin
  Subtractor #(.width(32)) subtractor_1 (
    .a(Entrada_A), .b(Entrada_B), .out(subResult), .bout(subtractor_1_bout));  // open: bin
  Shifter #(.width(32)) shifter_1 (.in(Entrada_B), .\dist (SHAMT), .out(SLL));
  Shifter #(.width(32), .shift("lr")) shifter_2 (.in(Entrada_B), .\dist (SHAMT), .out(SRL));
  // AND_Gate and_2 has open pins: in0=adder_1_cout, in1=isSum, out=open
  // AND_Gate and_3 has open pins: in0=subtractor_1_bout, in1=isSub, out=open
  Multiplexer #(.select(5), .width(32), .enable("false")) multiplexer_1 (
    .in0(SLL), .in2(SRL), .in16(sumResult), .in18(subResult), .in20(AND), .in21(OR), .in22(XOR), .in23(NOR),
    .in26({{31{1'b0}}, SLT[0]}), .out(Result), .sel(\Operação_ALU ));  // open: in1, in3, in4, in5, in6, in7, in8, in9, in10, in11, in12, in13, in14, in15, in17, in19, in24, in25, in27, in28, in29, in30, in31
  and and_4 (and_4_out, Entrada_A[31], Entrada_B[31], ~Result[31]);  // AND_Gate
  and and_5 (and_5_out, ~Entrada_A[31], ~Entrada_B[31], Result[31]);  // AND_Gate
  or or_2 (or_2_out, and_4_out, and_5_out);
  or or_3 (or_3_out, isSum, isSub);
  and and_6 (Overflow, or_2_out, or_3_out);
  and and_7 (isSum, ~\Operação_ALU [0], ~\Operação_ALU [1], ~\Operação_ALU [2], ~\Operação_ALU [3], \Operação_ALU [4]);  // AND_Gate
  and and_8 (isSub, ~\Operação_ALU [0], \Operação_ALU [1], ~\Operação_ALU [2], ~\Operação_ALU [3], \Operação_ALU [4]);  // AND_Gate
  nor nor_2 (Zero, Result[0], Result[1], Result[2], Result[3], Result[4], Result[5], Result[6], Result[7], Result[8], Result[9], Result[10], Result[11], Result[12], Result[13], Result[14], Result[15], Result[16], Result[17], Result[18], Result[19], Result[20], Result[21], Result[22], Result[23], Result[24], Result[25], Result[26], Result[27], Result[28], Result[29], Result[30], Result[31]);

  // Other names for the same wires on the sheet: A[31:0] = Entrada_A; B[31:0] = Entrada_B;
  //   opALU[4:0] = \Operação_ALU ; Result_Tunnel[31:0] = Result

  // Notes on the sheet:
  //   SLT
  //   ADD
  //   SUB
  //   SLL
  //   SRL
  //   10100 - AND = 20
  //   10101 - OR = 21
  //   10111 - NOR = 23
  //   10110 - XOR = 22
  //   11010 - SLT = 26
  //   10000 - ADD = 16
  //   10010 - SUB = 18
  //   00000 - SLL = 0
  //   00010 - SRL = 2
endmodule
