// Logisim project decodificador.circ as structural Verilog: 2 circuits, main circuit decodificador
module decodificador (
  input  [31:0] \INSTRUÇÃO ,
  output [5:0] OP_CODE,
  output [15:0] IMM,
  output [25:0] ADDR,
  output [4:0] RS,
  output [4:0] RT,
  output [4:0] RD,
  output [4:0] SHAMT,
  output [5:0] FUNC
);


  assign ADDR = \INSTRUÇÃO [25:0];
  assign FUNC = \INSTRUÇÃO [5:0];
  assign IMM = \INSTRUÇÃO [15:0];
  assign OP_CODE = \INSTRUÇÃO [31:26];
  assign RD = \INSTRUÇÃO [15:11];
  assign RS = \INSTRUÇÃO [25:21];
  assign RT = \INSTRUÇÃO [20:16];
  assign SHAMT = \INSTRUÇÃO [10:6];

  // Other names for the same wires on the sheet: OPCODE[5:0] = \INSTRUÇÃO [31:26]

  // Notes on the sheet:
  //   Instrução tipo R
  //   Instrução tipo I
  //   Instrução tipo J
endmodule

module extensor_sinal (
  input  [15:0] entrada,
  output [31:0] saida
);


  assign saida = {{17{entrada[15]}}, entrada[14:0]};
endmodule
