// Logisim project memdados.circ as structural Verilog: 1 circuit, main circuit datamem
// Mem. dados
module datamem (
  input  [31:0] \Endereço ,
  input  [31:0] Escreve_dado,
  input  clk,
  input  clear,
  input  MemWrite,
  input  MemRead,
  output [31:0] Dados_lidos
);

  wire [31:0] shifter_1_out;

  // Probe on \Endereço 
  Shifter #(.width(32), .shift("lr")) shifter_1 (.in(\Endereço ), .\dist (5'b00010), .out(shifter_1_out));
  // Probe on shifter_1_out
  // Probe on Escreve_dado
  RAM #(.addrWidth(24), .dataWidth(32), .bus("separate")) ram_1 (
    .addr(shifter_1_out[23:0]), .din(Escreve_dado), .data(Dados_lidos), .str(MemWrite), .clk(clk),
    .ld(MemRead), .clr(clear));  // open: sel
  // Probe on Dados_lidos
endmodule
