// Logisim project meminstr.circ as structural Verilog: 1 circuit, main circuit MemInstr
module MemInstr (
  input  [31:0] PC_address,
  output [31:0] Instruction
);

  // Probe on PC_address
  // Probe on PC_address[25:2]
  ROM #(.addrWidth(24), .dataWidth(32)) rom_1 (.addr(PC_address[25:2]), .data(Instruction));  // open: sel
  // Probe on Instruction

  // Notes on the sheet:
  //   contents of rom_1 (hex, n*v repeats v):
  //   23bd1fff 8100000 1048574*0 20040000 20050005 c100004 8100031 23bdffec afbf0010 afb3000c afb20008
  //   afb10004 afb00000 49020 20b3ffff 8020 213082a 10200014 8820 2704022 228482a 200a0001 152a000d 114080
  //   2484820 8d290000 22280001 84080 2485020 8d4a0000 149082a 10200002 2202820 c10002a 22310001 8100010
  //   22100001 810000d 8fb00000 8fb10004 8fb20008 8fb3000c 8fbf0010 23bd0014 3e00008 54880 894820 8d280000
  //   8d2a0004 ad2a0000 ad280004 3e00008
endmodule
